// Logisim project AndOrNot.circ as structural Verilog: 1 circuit, main circuit main
module main (
);

  wire and_1_out, not_1_out, or_1_out, undriven, undriven_2, undriven_3, undriven_4, undriven_5;

  and and_1 (and_1_out, undriven, undriven_2);
  or or_1 (or_1_out, undriven_3, undriven_4);
  not not_1 (not_1_out, undriven_5);

  // Notes on the sheet:
  //   p
  //   q
  //   p
  //   q
  //   p
  //   AND
  //   OR
  //   NOT
  //   pq
  //   p+q
  //   p̅
endmodule
