// Logisim project DELatchSymbol.circ as structural Verilog: 2 circuits, main circuit main
module DElatch (
  input  D,
  input  E,
  output Q,
  output out_4
);

  wire nand_1_out, nand_2_out;

  nand nand_1 (nand_1_out, D, E);
  nand nand_2 (nand_2_out, nand_1_out, E);
  nand nand_3 (Q, nand_1_out, out_4);
  nand nand_4 (out_4, Q, nand_2_out);
endmodule

module main (
);

  wire delatch_1_out_4, delatch_1_q, undriven, undriven_2;

  DElatch delatch_1 (.D(undriven), .E(undriven_2), .Q(delatch_1_q), .out_4(delatch_1_out_4));
endmodule
