// Logisim project DEMUX.circ as structural Verilog: 2 circuits, main circuit demux
module demux (
  input  in_1,
  input  in_2,
  input  in_3,
  output out_4,
  output out_5,
  output out_6,
  output out_7
);
endmodule

module main (
);

  wire demux_1_out_4, demux_1_out_5, demux_1_out_6, demux_1_out_7, undriven, undriven_2, undriven_3;

  demux demux_1 (
    .in_1(undriven), .out_4(demux_1_out_4), .out_5(demux_1_out_5), .out_6(demux_1_out_6),
    .out_7(demux_1_out_7), .in_2(undriven_2), .in_3(undriven_3));

  // Notes on the sheet:
  //   a
  //   s1
  //   s0
  //   x00
  //   x01
  //   x10
  //   x11
endmodule
