// Logisim project DFlipFlop.circ as structural Verilog: 2 circuits, main circuit DFlipFlop
module DFlipFlop (
  input  Clk,
  input  D,
  output Q,
  output Q_prime
);

  wire nand_1_out, nand_2_out, nand_3_out, nand_4_out;

  nand nand_1 (nand_1_out, nand_4_out, nand_2_out);
  nand nand_2 (nand_2_out, nand_1_out, Clk);
  nand nand_3 (nand_3_out, nand_2_out, Clk, nand_4_out);
  nand nand_4 (nand_4_out, nand_3_out, D);
  nand nand_5 (Q, nand_2_out, Q_prime);
  nand nand_6 (Q_prime, Q, nand_3_out);

  // Notes on the sheet:
  //   x
  //   S̅
  //   R̅
  //   y
endmodule

module main (
);

  wire dflipflop_1_q, dflipflop_1_q_prime, undriven, undriven_2;

  DFlipFlop dflipflop_1 (.Clk(undriven_2), .D(undriven), .Q(dflipflop_1_q), .Q_prime(dflipflop_1_q_prime));
endmodule
