// Logisim project DNFlayers.circ as structural Verilog: 1 circuit, main circuit main
module main (
);

  wire and_1_out, and_2_out, and_3_out, not_1_out, not_2_out, or_1_out, undriven, undriven_2, undriven_3,
       undriven_4, undriven_5, undriven_6, undriven_7, undriven_8, undriven_9, undriven_10, undriven_11;

  not not_1 (not_1_out, undriven);
  not not_2 (not_2_out, undriven_2);
  and and_1 (and_1_out, undriven_3, undriven_4, undriven_5);
  and and_2 (and_2_out, undriven_6, undriven_7, undriven_8);
  and and_3 (and_3_out, undriven_9, undriven_10, undriven_11);
  or or_1 (or_1_out, and_1_out, and_2_out, and_3_out);

  // Notes on the sheet:
  //   a
  //   b
  //   ...
  //   connect
  //   literals
  //   here
  //   ...
  //   x
endmodule
