// Logisim project DNFlayersNand.circ as structural Verilog: 1 circuit, main circuit main
module main (
);

  wire nand_1_out, nand_2_out, nand_3_out, nand_4_out, not_1_out, not_2_out, undriven, undriven_2,
       undriven_3, undriven_4, undriven_5, undriven_6, undriven_7, undriven_8, undriven_9, undriven_10,
       undriven_11;

  not not_1 (not_1_out, undriven);
  not not_2 (not_2_out, undriven_2);
  nand nand_1 (nand_1_out, undriven_3, undriven_4, undriven_5);
  nand nand_2 (nand_2_out, undriven_6, undriven_7, undriven_8);
  nand nand_3 (nand_3_out, undriven_9, undriven_10, undriven_11);
  nand nand_4 (nand_4_out, nand_1_out, nand_2_out, nand_3_out);

  // Notes on the sheet:
  //   a
  //   b
  //   ...
  //   connect
  //   literals
  //   here
  //   ...
  //   x
endmodule
