// Logisim project Exercise5213b.circ as structural Verilog: 1 circuit, main circuit main
module main (
);

  wire not_1_out, not_2_out, not_3_out, not_4_out, not_5_out, or_1_out, or_2_out, or_3_out, undriven,
       undriven_2;

  not not_1 (not_1_out, undriven);
  not not_2 (not_2_out, undriven_2);
  not not_3 (not_3_out, or_1_out);
  or or_1 (or_1_out, not_1_out, undriven_2);
  not not_4 (not_4_out, or_2_out);
  or or_2 (or_2_out, undriven, not_2_out);
  or or_3 (or_3_out, not_3_out, not_4_out);
  not not_5 (not_5_out, or_3_out);

  // Notes on the sheet:
  //   a
  //   b
  //   x
endmodule
