// Logisim project ForG.circ as structural Verilog: 3 circuits, main circuit main
module main (
);

  wire and_1_out, and_2_out, f_1_out_4, g_1_out_4, not_1_out, or_1_out, undriven, undriven_2, undriven_3,
       undriven_4;

  f f_1 (.in_1(undriven), .in_2(undriven_2), .in_3(undriven_3), .out_4(f_1_out_4));
  g g_1 (.in_1(undriven), .in_2(undriven_2), .in_3(undriven_3), .out_4(g_1_out_4));
  not not_1 (not_1_out, undriven_4);
  and and_1 (and_1_out, f_1_out_4, not_1_out);
  and and_2 (and_2_out, undriven_4, g_1_out_4);
  or or_1 (or_1_out, and_1_out, and_2_out);

  // Notes on the sheet:
  //   inputs
  //   select
  //   output
endmodule

module f (
  input  in_1,
  input  in_2,
  input  in_3,
  output out_4
);
endmodule

module g (
  input  in_1,
  input  in_2,
  input  in_3,
  output out_4
);
endmodule
