// Logisim project FullAdder.circ as structural Verilog: 5 circuits, main circuit HalfAdder
module HalfAdder (
  input  a,
  input  b,
  output s,
  output c
);

  wire not_1_out, or_1_out;

  or or_1 (or_1_out, a, b);
  and and_1 (c, a, b);
  not not_1 (not_1_out, c);
  and and_2 (s, or_1_out, not_1_out);
endmodule

module FullAdder (
);

  wire fasymbol_1_cout, fasymbol_1_s, halfadder_1_c, halfadder_1_s, halfadder_2_c, halfadder_2_s, or_1_out,
       undriven, undriven_2, undriven_3, undriven_4, undriven_5, undriven_6;

  HalfAdder halfadder_1 (.a(undriven), .b(halfadder_2_s), .s(halfadder_1_s), .c(halfadder_1_c));
  HalfAdder halfadder_2 (.a(undriven_2), .b(undriven_3), .s(halfadder_2_s), .c(halfadder_2_c));
  FASymbol fasymbol_1 (.cin(undriven_4), .a(undriven_5), .b(undriven_6), .s(fasymbol_1_s), .cout(fasymbol_1_cout));
  or or_1 (or_1_out, halfadder_1_c, halfadder_2_c);

  // Notes on the sheet:
  //   cin
  //   a
  //   b
  //   s
  //   cout
endmodule

module main (
);

  wire halfadder_1_c, halfadder_1_s, undriven, undriven_2;

  HalfAdder halfadder_1 (.a(undriven), .b(undriven_2), .s(halfadder_1_s), .c(halfadder_1_c));
endmodule

module FASymbol (
  input  cin,
  input  a,
  input  b,
  output s,
  output cout
);
endmodule

module _4BitAdder (
);

  wire fasymbol_1_cout, fasymbol_1_s, fasymbol_2_cout, fasymbol_2_s, fasymbol_3_cout, fasymbol_3_s,
       fasymbol_4_cout, fasymbol_4_s, undriven, undriven_2, undriven_3, undriven_4, undriven_5, undriven_6,
       undriven_7, undriven_8, undriven_9;

  FASymbol fasymbol_1 (.cin(undriven), .a(undriven_2), .b(undriven_3), .s(fasymbol_1_s), .cout(fasymbol_1_cout));
  FASymbol fasymbol_2 (.cin(fasymbol_1_cout), .a(undriven_4), .b(undriven_5), .s(fasymbol_2_s), .cout(fasymbol_2_cout));
  FASymbol fasymbol_3 (.cin(fasymbol_2_cout), .a(undriven_6), .b(undriven_7), .s(fasymbol_3_s), .cout(fasymbol_3_cout));
  FASymbol fasymbol_4 (.cin(fasymbol_3_cout), .a(undriven_8), .b(undriven_9), .s(fasymbol_4_s), .cout(fasymbol_4_cout));

  // Notes on the sheet:
  //   cin
  //   a0
  //   b0
  //   a1
  //   b1
  //   a2
  //   b2
  //   a3
  //   b3
  //   s0
  //   s1
  //   s2
  //   s3
  //   cout
endmodule
