// Logisim project HalfAdder11.circ as structural Verilog: 1 circuit, main circuit main
module main (
);

  wire and_1_out, and_2_out, not_1_out, or_1_out, undriven, undriven_2;

  or or_1 (or_1_out, undriven, undriven_2);
  and and_1 (and_1_out, undriven, undriven_2);
  not not_1 (not_1_out, and_1_out);
  and and_2 (and_2_out, or_1_out, not_1_out);

  // Notes on the sheet:
  //   a
  //   b
  //   1
  //   1
  //   1
  //   1
  //   0
  //   0
  //   s
  //   c
  //   1
endmodule
