// Logisim project MUX.circ as structural Verilog: 2 circuits, main circuit main
module main (
);

  wire and_1_out, and_2_out, and_3_out, and_4_out, muxsymbol_1_out_7, not_1_out, not_2_out, or_1_out,
       undriven, undriven_2, undriven_3, undriven_4, undriven_5, undriven_6, undriven_7, undriven_8,
       undriven_9, undriven_10, undriven_11, undriven_12;

  not not_1 (not_1_out, undriven_5);
  and and_1 (and_1_out, undriven, not_1_out, not_2_out);
  and and_2 (and_2_out, undriven_2, not_1_out, undriven_6);
  and and_3 (and_3_out, undriven_3, undriven_5, not_2_out);
  and and_4 (and_4_out, undriven_4, undriven_5, undriven_6);
  not not_2 (not_2_out, undriven_6);
  or or_1 (or_1_out, and_1_out, and_2_out, and_3_out, and_4_out);
  MUXSymbol muxsymbol_1 (
    .in_1(undriven_7), .in_2(undriven_8), .in_3(undriven_9), .in_4(undriven_10), .out_7(muxsymbol_1_out_7),
    .in_5(undriven_11), .in_6(undriven_12));

  // Notes on the sheet:
  //   a00
  //   a01
  //   a10
  //   a11
  //   s1
  //   s0
  //   a00
  //   a01
  //   a10
  //   a11
  //   x
  //   s0
  //   s1
  //   x
endmodule

module MUXSymbol (
  input  in_1,
  input  in_2,
  input  in_3,
  input  in_4,
  input  in_5,
  input  in_6,
  output out_7
);
endmodule
