// Logisim project Mod3Counter.circ as structural Verilog: 2 circuits, main circuit DFlipFlop
module DFlipFlop (
  input  Clk,
  input  D,
  output Q,
  output Q_prime
);

  wire nand_1_out, nand_2_out, nand_3_out, nand_4_out;

  nand nand_1 (nand_1_out, nand_4_out, nand_2_out);
  nand nand_2 (nand_2_out, nand_1_out, Clk);
  nand nand_3 (nand_3_out, nand_2_out, Clk, nand_4_out);
  nand nand_4 (nand_4_out, nand_3_out, D);
  nand nand_5 (Q, nand_2_out, Q_prime);
  nand nand_6 (Q_prime, Q, nand_3_out);

  // Notes on the sheet:
  //   x
  //   S̅
  //   R̅
  //   y
endmodule

module main (
);

  wire and_1_out, and_2_out, and_3_out, and_4_out, and_5_out, not_1_out, or_1_out, or_2_out, Q0_q,
       Q0_q_prime, Q1_q, Q1_q_prime, undriven, undriven_2;

  not not_1 (not_1_out, undriven);
  and and_1 (and_1_out, Q1_q_prime, Q0_q_prime);
  and and_2 (and_2_out, and_1_out, undriven);
  and and_3 (and_3_out, not_1_out, Q0_q);
  and and_4 (and_4_out, and_1_out, not_1_out);
  and and_5 (and_5_out, undriven, Q1_q);
  or or_1 (or_1_out, and_2_out, and_3_out);
  or or_2 (or_2_out, and_4_out, and_5_out);
  DFlipFlop Q1 (.Clk(undriven_2), .D(or_1_out), .Q(Q1_q), .Q_prime(Q1_q_prime));
  DFlipFlop Q0 (.Clk(undriven_2), .D(or_2_out), .Q(Q0_q), .Q_prime(Q0_q_prime));

  // Notes on the sheet:
  //   a
  //   Clock
  //   x1
  //   x0
endmodule
