// Logisim project MooreMachine.circ as structural Verilog: 3 circuits, main circuit main
module main (
);

  wire combo_1_out_3, combo_1_out_4, state_1_out_3, undriven, undriven_2;

  Combo combo_1 (.in_1(undriven), .in_2(state_1_out_3), .out_3(combo_1_out_3), .out_4(combo_1_out_4));
  State state_1 (.in_1(combo_1_out_4), .in_2(undriven_2), .out_3(state_1_out_3));

  // Notes on the sheet:
  //   Input
  //   Clock
  //   Output
endmodule

module State (
  input  in_1,
  input  in_2,
  output out_3
);
endmodule

module Combo (
  input  in_1,
  input  in_2,
  output out_3,
  output out_4
);
endmodule
