// Logisim project NMOSgates.circ as structural Verilog: 1 circuit, main circuit main
module main (
);

  wire pull_resistor_1_node, pull_resistor_2_node, pull_resistor_3_node, transistor_5_out, undriven,
       undriven_2, undriven_3;

  Pull_Resistor #(.pull(1)) pull_resistor_1 (.node(pull_resistor_1_node));
  Transistor #(.\type ("n")) transistor_1 (.in(1'b0), .out(pull_resistor_1_node), .gate(undriven));
  Pull_Resistor #(.pull(1)) pull_resistor_2 (.node(pull_resistor_2_node));
  Transistor #(.\type ("n")) transistor_2 (.in(1'b0), .out(pull_resistor_2_node));  // open: gate
  Transistor #(.\type ("n")) transistor_3 (.in(1'b0), .out(pull_resistor_2_node));  // open: gate
  Pull_Resistor #(.pull(1)) pull_resistor_3 (.node(pull_resistor_3_node));
  Transistor #(.\type ("n")) transistor_4 (.in(transistor_5_out), .out(pull_resistor_3_node), .gate(undriven_2));
  Transistor #(.\type ("n")) transistor_5 (.in(1'b0), .out(transistor_5_out), .gate(undriven_3));

  // Notes on the sheet:
  //   a
  //   a̅
  //   a
  //   b
  //   a↓b
  //   a
  //   b
  //   a↑b
endmodule
