// Logisim project NandNor.circ as structural Verilog: 1 circuit, main circuit main
module main (
);

  wire nand_1_out, nor_1_out, undriven, undriven_2, undriven_3, undriven_4;

  nand nand_1 (nand_1_out, undriven, undriven_2);
  nor nor_1 (nor_1_out, undriven_3, undriven_4);

  // Notes on the sheet:
  //   p
  //   q
  //   p
  //   q
  //   NAND
  //   NOR
  //   p↑q
  //   p↓q
endmodule
