// Logisim project NotLatch.circ as structural Verilog: 1 circuit, main circuit main
module main (
);

  wire not_1_out, not_2_out;

  not not_1 (not_1_out, not_2_out);
  not not_2 (not_2_out, not_1_out);

  // Notes on the sheet:
  //   x
  //   y
endmodule
