// Logisim project SRLatch.circ as structural Verilog: 1 circuit, main circuit main
module main (
);

  wire nand_1_out, nand_2_out, undriven, undriven_2;

  nand nand_1 (nand_1_out, undriven, nand_2_out);
  nand nand_2 (nand_2_out, nand_1_out, undriven_2);

  // Notes on the sheet:
  //   S̅
  //   R̅
  //   Q
  //   Q̅
endmodule
