// Logisim project XOR.circ as structural Verilog: 1 circuit, main circuit main
module main (
);

  wire undriven, undriven_2, xor_1_out;

  xor xor_1 (xor_1_out, undriven, undriven_2);

  // Notes on the sheet:
  //   p
  //   q
  //   XOR
  //   p⊕q
endmodule
